// Logisim project transistor-level.circ as structural Verilog: 4 circuits, main circuit main
module main (
  input  A,
  input  B,
  input  in_3,
  input  in_4,
  output Z
);

  a a_1 (.A(A), .B(B), .Z(Z));
  b b_1 (.A(A), .B(B), .Z(Z));
  c c_1 (.A(A), .B(B), .Z(Z));
  // AND_Gate and_1 has open pins: in0=in_3, in1=in_4, out=open
endmodule

module a (
  input  A,
  input  B,
  output Z
);

  wire transistor_1_out, transistor_3_out, transistor_5_out, transistor_8_out, transistor_9_out,
       transistor_12_out, transistor_13_out, transistor_15_out, transistor_17_out, transistor_18_out;

  Transistor transistor_1 (.in(1'b1), .out(transistor_1_out), .gate(A));
  Transistor #(.\type ("n")) transistor_2 (.in(1'b0), .out(transistor_1_out), .gate(A));
  Transistor transistor_3 (.in(1'b1), .out(transistor_3_out), .gate(B));
  Transistor #(.\type ("n")) transistor_4 (.in(1'b0), .out(transistor_3_out), .gate(B));
  Transistor transistor_5 (.in(1'b1), .out(transistor_5_out), .gate(A));
  Transistor transistor_6 (.in(1'b1), .out(transistor_5_out), .gate(B));
  Transistor #(.\type ("n")) transistor_7 (.in(transistor_8_out), .out(transistor_5_out), .gate(A));
  Transistor #(.\type ("n")) transistor_8 (.in(1'b0), .out(transistor_8_out), .gate(B));
  Transistor transistor_9 (.in(1'b1), .out(transistor_9_out), .gate(transistor_3_out));
  Transistor transistor_10 (.in(1'b1), .out(transistor_9_out), .gate(transistor_1_out));
  Transistor #(.\type ("n")) transistor_11 (.in(transistor_12_out), .out(transistor_9_out), .gate(transistor_3_out));
  Transistor #(.\type ("n")) transistor_12 (.in(1'b0), .out(transistor_12_out), .gate(transistor_1_out));
  Transistor transistor_13 (.in(1'b1), .out(transistor_13_out), .gate(transistor_5_out));
  Transistor #(.\type ("n")) transistor_14 (.in(1'b0), .out(transistor_13_out), .gate(transistor_5_out));
  Transistor transistor_15 (.in(1'b1), .out(transistor_15_out), .gate(transistor_9_out));
  Transistor #(.\type ("n")) transistor_16 (.in(1'b0), .out(transistor_15_out), .gate(transistor_9_out));
  Transistor transistor_17 (.in(1'b1), .out(transistor_17_out), .gate(transistor_13_out));
  Transistor transistor_18 (.in(transistor_17_out), .out(transistor_18_out), .gate(transistor_15_out));
  Transistor #(.\type ("n")) transistor_19 (.in(1'b0), .out(transistor_18_out), .gate(transistor_15_out));
  Transistor #(.\type ("n")) transistor_20 (.in(1'b0), .out(transistor_18_out), .gate(transistor_13_out));
  Transistor transistor_21 (.in(1'b1), .out(Z), .gate(transistor_18_out));
  Transistor #(.\type ("n")) transistor_22 (.in(1'b0), .out(Z), .gate(transistor_18_out));

  // Notes on the sheet:
  //   AND
  //   NOT
  //   NOT
  //   AND
  //   OR
endmodule

module b (
  input  A,
  input  B,
  output Z
);

  wire transistor_1_out, transistor_4_out, transistor_5_out, transistor_6_out, transistor_8_out,
       transistor_13_out, transistor_16_out;

  Transistor transistor_1 (.in(1'b1), .out(transistor_1_out), .gate(A));
  Transistor transistor_2 (.in(1'b1), .out(transistor_1_out), .gate(B));
  Transistor #(.\type ("n")) transistor_3 (.in(transistor_4_out), .out(transistor_1_out), .gate(A));
  Transistor #(.\type ("n")) transistor_4 (.in(1'b0), .out(transistor_4_out), .gate(B));
  Transistor transistor_5 (.in(1'b1), .out(transistor_5_out), .gate(B));
  Transistor transistor_6 (.in(1'b1), .out(transistor_6_out), .gate(transistor_5_out));
  Transistor #(.\type ("n")) transistor_7 (.in(1'b0), .out(transistor_5_out), .gate(B));
  Transistor transistor_8 (.in(1'b1), .out(transistor_8_out), .gate(A));
  Transistor #(.\type ("n")) transistor_9 (.in(1'b0), .out(transistor_8_out), .gate(A));
  Transistor transistor_10 (.in(1'b1), .out(Z), .gate(transistor_1_out));
  Transistor transistor_11 (.in(1'b1), .out(transistor_6_out), .gate(transistor_8_out));
  Transistor #(.\type ("n")) transistor_12 (.in(transistor_13_out), .out(transistor_6_out), .gate(transistor_5_out));
  Transistor #(.\type ("n")) transistor_13 (.in(1'b0), .out(transistor_13_out), .gate(transistor_8_out));
  Transistor transistor_14 (.in(1'b1), .out(Z), .gate(transistor_6_out));
  Transistor #(.\type ("n")) transistor_15 (.in(transistor_16_out), .out(Z), .gate(transistor_1_out));
  Transistor #(.\type ("n")) transistor_16 (.in(1'b0), .out(transistor_16_out), .gate(transistor_6_out));
endmodule

module c (
  input  A,
  input  B,
  output Z
);

  wire transistor_1_out, transistor_3_out;

  Transistor transistor_1 (.in(1'b1), .out(transistor_1_out), .gate(A));
  Transistor #(.\type ("n")) transistor_2 (.in(1'b0), .out(transistor_1_out), .gate(A));
  Transistor transistor_3 (.in(1'b1), .out(transistor_3_out), .gate(B));
  Transistor #(.\type ("n")) transistor_4 (.in(1'b0), .out(transistor_3_out), .gate(B));
  Transistor transistor_5 (.in(B), .out(Z), .gate(transistor_1_out));
  Transistor #(.gate("br"), .\type ("n")) transistor_6 (.in(B), .out(Z), .gate(A));
  Transistor transistor_7 (.in(transistor_3_out), .out(Z), .gate(A));
  Transistor #(.gate("br"), .\type ("n")) transistor_8 (.in(transistor_3_out), .out(Z), .gate(transistor_1_out));
endmodule
